// Logisim project ARQI_main_Add_1_Add_2.circ as structural Verilog: 3 circuits, main circuit main
module main (
  input  A,
  input  B,
  input  C__Vem_1,
  output Vai_1,
  output S
);

  Add_1 add_1_1 (.S(S), .Vai_1(Vai_1), .A(A), .B(B), .C__Vem_1(C__Vem_1));
endmodule

module Add_1 (
  input  A,
  input  B,
  input  C__Vem_1,
  output S,
  output Vai_1
);

  wire and_1_out, and_2_out, or_1_out, xor_1_out;

  or or_1 (or_1_out, C__Vem_1, B);
  xor xor_1 (xor_1_out, B, C__Vem_1);
  and and_1 (and_1_out, or_1_out, A);
  and and_2 (and_2_out, B, C__Vem_1);
  xor xor_2 (S, xor_1_out, A);
  or or_2 (Vai_1, and_1_out, and_2_out);

  // Notes on the sheet:
  //   S = A XOR (B XOR C)
endmodule

module Add_2 (
  input  A,
  input  B,
  input  A_2,
  input  B_2,
  output Overflow,
  output [1:0] out_6
);

  wire add_1_2_vai_1;

  Add_1 add_1_1 (.S(out_6[1]), .Vai_1(Overflow), .A(A), .B(B), .C__Vem_1(add_1_2_vai_1));
  Add_1 add_1_2 (.S(out_6[0]), .Vai_1(add_1_2_vai_1), .A(A_2), .B(B_2), .C__Vem_1(1'b0));
endmodule
