// Logisim project CONVERSOR_BCD P 7 SEG.circ as structural Verilog: 2 circuits, main circuit main
module main (
);

  _7_Segment_Display u_7_segment_display_1 ();  // open: g, f, a, b, e, d, c, dp
endmodule

module CONVERSOR_BCD (
  input  A,
  input  B,
  input  C,
  input  D,
  input  B_2,
  input  C_2,
  input  D_2,
  input  A_2,
  input  B_3,
  input  C_3,
  input  D_3,
  input  A_3,
  input  A_4,
  input  B_4,
  input  B_5,
  input  C_4,
  input  C_5,
  input  D_4,
  input  D_5,
  output out_20,
  output e,
  output c___B___C_prime___D,
  output out_23,
  output f,
  output d_6,
  output out_26
);

  wire and_1_out, and_2_out, and_3_out, and_5_out, and_6_out, not_1_out, not_2_out, not_3_out, not_4_out,
       not_5_out, not_7_out, not_8_out, not_9_out, not_10_out, not_11_out, not_12_out, not_13_out, or_1_out,
       or_2_out, or_7_out, or_8_out, or_9_out, xnor_1_out, xor_1_out, xor_2_out;

  not not_1 (not_1_out, B_4);
  or or_1 (or_1_out, C_4, not_2_out);
  not not_2 (not_2_out, D_4);
  not not_3 (not_3_out, D_4);
  xor xor_1 (xor_1_out, B, D);
  not not_4 (not_4_out, B);
  xnor xnor_1 (xnor_1_out, C, D);
  not not_5 (not_5_out, C);
  and and_1 (and_1_out, not_1_out, or_1_out);
  not not_6 (and_1_out, D_4);
  and and_2 (and_2_out, C_4, not_3_out);
  or or_2 (or_2_out, A, not_7_out);
  not not_7 (not_7_out, xor_1_out);
  or or_3 (c___B___C_prime___D, not_4_out, xnor_1_out);
  and and_3 (and_3_out, B_4, C_4, and_1_out);
  or or_4 (out_20, or_2_out, C);
  or or_5 (out_23, B, not_5_out, D);
  or or_6 (d_6, A_3, and_3_out, and_1_out, and_2_out);
  not not_8 (not_8_out, B_2);
  not not_9 (not_9_out, D_2);
  not not_10 (not_10_out, D_3);
  not not_11 (not_11_out, D_3);
  not not_12 (not_12_out, D_5);
  or or_7 (or_7_out, not_8_out, C_2);
  and and_4 (e, or_7_out, not_9_out);
  or or_8 (or_8_out, not_10_out, B_3);
  not not_13 (not_13_out, C_3);
  or or_9 (or_9_out, B_3, not_11_out);
  xor xor_2 (xor_2_out, B_5, C_5);
  and and_5 (and_5_out, C_5, not_12_out);
  and and_6 (and_6_out, or_8_out, not_13_out);
  or or_10 (out_26, A_4, xor_2_out, and_5_out);
  or or_11 (f, A_2, and_6_out, or_9_out);

  // Notes on the sheet:
  //   d = A + CD' + BD'C + B'(C+D')
  //   b = B' + (C ouisclusivo D)'
  //   a = C + A + (B osclisiovpo D)'
  //   e = D' º (C + B')
  //   f = A + C' (D' + B) + BD'
  //   g = CD' + A + B ouisclusivo C
endmodule
