// Logisim project CONVERSOR_BCD_7 SEG_ComVerificador.circ as structural Verilog: 2 circuits, main circuit main
module main (
  input  in_1,
  input  in_2,
  input  in_3,
  input  in_4
);

  wire conversor_bcd_1_out_5, conversor_bcd_1_out_6, conversor_bcd_1_out_7, conversor_bcd_1_out_8,
       conversor_bcd_1_out_9, conversor_bcd_1_out_10, conversor_bcd_1_out_11;

  CONVERSOR_BCD conversor_bcd_1 (
    .A(in_1), .B(in_2), .C(in_3), .out_6(conversor_bcd_1_out_6), .out_7(conversor_bcd_1_out_7),
    .out_5(conversor_bcd_1_out_5), .D(in_4), .out_8(conversor_bcd_1_out_8), .out_10(conversor_bcd_1_out_10),
    .out_9(conversor_bcd_1_out_9), .out_11(conversor_bcd_1_out_11));
  _7_Segment_Display u_7_segment_display_1 (
    .g(conversor_bcd_1_out_11), .f(conversor_bcd_1_out_10), .a(conversor_bcd_1_out_5),
    .b(conversor_bcd_1_out_6), .e(conversor_bcd_1_out_9), .d(conversor_bcd_1_out_8),
    .c(conversor_bcd_1_out_7), .dp(1'b0));
  LED led_1 ();  // open: in
  LED led_2 ();  // open: in
  LED led_3 ();  // open: in
  LED led_4 ();  // open: in
endmodule

module CONVERSOR_BCD (
  input  A,
  input  B,
  input  C,
  input  D,
  output out_5,
  output out_6,
  output out_7,
  output out_8,
  output out_9,
  output out_10,
  output out_11
);

  wire and_1_out, and_2_out, and_3_out, and_4_out, and_5_out, and_6_out, and_7_out, and_15_out, not_1_out,
       not_2_out, not_3_out, not_4_out, not_5_out, not_6_out, not_7_out, not_8_out, not_9_out, not_10_out,
       not_11_out, not_12_out, not_13_out, not_14_out, or_1_out, or_2_out, or_3_out, or_4_out, or_5_out,
       or_6_out, or_7_out, or_8_out, or_9_out, or_10_out, or_11_out, xnor_1_out, xor_1_out, xor_2_out;

  not not_1 (not_1_out, xor_1_out);
  xor xor_1 (xor_1_out, B, D);
  not not_2 (not_2_out, B);
  xnor xnor_1 (xnor_1_out, C, D);
  or or_1 (or_1_out, B, not_3_out, D);
  not not_3 (not_3_out, C);
  not not_4 (not_4_out, C);
  not not_5 (not_5_out, B);
  or or_2 (or_2_out, C, not_6_out);
  not not_6 (not_6_out, D);
  and and_1 (and_1_out, C, not_7_out);
  not not_7 (not_7_out, D);
  not not_8 (not_8_out, B);
  or or_3 (or_3_out, not_8_out, C);
  not not_9 (not_9_out, D);
  not not_10 (not_10_out, D);
  and and_2 (and_2_out, not_10_out, B);
  not not_11 (not_11_out, C);
  or or_4 (or_4_out, B, not_12_out);
  not not_12 (not_12_out, D);
  xor xor_2 (xor_2_out, B, C);
  and and_3 (and_3_out, C, not_13_out);
  not not_13 (not_13_out, D);
  or or_5 (or_5_out, A, not_1_out);
  or or_6 (or_6_out, not_2_out, xnor_1_out);
  and and_4 (and_4_out, B, not_4_out, D);
  and and_5 (and_5_out, not_5_out, or_2_out);
  and and_6 (and_6_out, or_3_out, not_9_out);
  or or_7 (or_7_out, A, and_2_out, and_7_out);
  and and_7 (and_7_out, not_11_out, or_4_out);
  or or_8 (or_8_out, A, xor_2_out, and_3_out);
  or or_9 (or_9_out, or_5_out, C);
  or or_10 (or_10_out, A, and_4_out, and_5_out, and_1_out);
  and and_8 (out_5, or_9_out, not_14_out);
  and and_9 (out_6, or_6_out, not_14_out);
  and and_10 (out_7, or_1_out, not_14_out);
  and and_11 (out_8, or_10_out, not_14_out);
  and and_12 (out_9, and_6_out, not_14_out);
  and and_13 (out_10, or_7_out, not_14_out);
  and and_14 (out_11, or_8_out, not_14_out);
  or or_11 (or_11_out, B, C);
  and and_15 (and_15_out, A, or_11_out);
  not not_14 (not_14_out, and_15_out);

  // Notes on the sheet:
  //   c = B + C' + D
  //   a = C + A + (B ouexclusivo D)'
  //   b = B' + (C ouisclusivo D)'
  //   d = A + CD' + BC'D + B'(C+D')
  //   e = D' º (C + B')
  //   f = A + C' (D' + B) + BD'
  //   g = CD' + A + B ouisclusivo C
  //   A
  //   B
  //   C
  //   if = 1 => Inválido
  //   Verificador de Saída Inválida [10, 15]
endmodule
