// Logisim project Somador de 4 bits.circ as structural Verilog: 3 circuits, main circuit main
module main (
  output [3:0] out_1
);

  add_4 add_4_1 (.out_4(out_1));  // open: in_2, Overflow, in_1
endmodule

module add_1 (
  input  a,
  input  b,
  input  Vem_1,
  output S,
  output Vai_1
);

  wire and_1_out, and_2_out, or_1_out, xor_1_out;

  xor xor_1 (xor_1_out, b, a);
  or or_1 (or_1_out, Vem_1, b);
  and and_1 (and_1_out, b, Vem_1);
  and and_2 (and_2_out, or_1_out, a);
  xor xor_2 (S, Vem_1, xor_1_out);
  or or_2 (Vai_1, and_2_out, and_1_out);
endmodule

module add_4 (
  input  [3:0] in_1,
  input  [3:0] in_2,
  output Overflow,
  output [3:0] out_4
);

  wire add_1_2_vai_1, add_1_3_vai_1, add_1_4_vai_1;

  // Probe on in_2
  add_1 add_1_1 (.S(out_4[3]), .Vai_1(Overflow), .a(in_2[3]), .b(in_1[3]), .Vem_1(add_1_3_vai_1));
  add_1 add_1_2 (.S(out_4[1]), .Vai_1(add_1_2_vai_1), .a(in_2[1]), .b(in_1[1]), .Vem_1(add_1_4_vai_1));
  add_1 add_1_3 (.S(out_4[2]), .Vai_1(add_1_3_vai_1), .a(in_2[2]), .b(in_1[2]), .Vem_1(add_1_2_vai_1));
  add_1 add_1_4 (.S(out_4[0]), .Vai_1(add_1_4_vai_1), .a(in_2[0]), .b(in_1[0]), .Vem_1(1'b0));
  // Probe on in_1
endmodule
