// Logisim project Subtrator.circ as structural Verilog: 5 circuits, main circuit main
module main (
  input  [3:0] entrada,
  input  overflow,
  output [3:0] \saída 
);

  // Probe on entrada
  COMPL_2 compl_2_1 (.in_1(entrada), .in_2(overflow), .S__Resultado(\saída ));
  // Probe on \saída 
endmodule

module add_1 (
  input  a,
  input  b,
  input  Vem_1,
  output S,
  output Vai_1
);

  wire and_1_out, and_2_out, or_1_out, xor_1_out;

  xor xor_1 (xor_1_out, b, a);
  or or_1 (or_1_out, Vem_1, b);
  and and_1 (and_1_out, b, Vem_1);
  and and_2 (and_2_out, or_1_out, a);
  xor xor_2 (S, Vem_1, xor_1_out);
  or or_2 (Vai_1, and_2_out, and_1_out);
endmodule

module add_4 (
  input  [3:0] in_1,
  input  [3:0] in_2,
  output Overflow,
  output [3:0] out_4
);

  wire add_1_2_vai_1, add_1_3_vai_1, add_1_4_vai_1;

  // Probe on in_2
  add_1 add_1_1 (.S(out_4[3]), .Vai_1(Overflow), .a(in_2[3]), .b(in_1[3]), .Vem_1(add_1_3_vai_1));
  add_1 add_1_2 (.S(out_4[1]), .Vai_1(add_1_2_vai_1), .a(in_2[1]), .b(in_1[1]), .Vem_1(add_1_4_vai_1));
  add_1 add_1_3 (.S(out_4[2]), .Vai_1(add_1_3_vai_1), .a(in_2[2]), .b(in_1[2]), .Vem_1(add_1_2_vai_1));
  add_1 add_1_4 (.S(out_4[0]), .Vai_1(add_1_4_vai_1), .a(in_2[0]), .b(in_1[0]), .Vem_1(1'b0));
  // Probe on in_1
endmodule

module COMPL_2 (
  input  [3:0] in_1,
  input  in_2,
  output [3:0] S__Resultado
);

  wire [3:0] not_1_out;

  not not_1 (not_1_out[0], in_1[0]);
  not not_2 (not_1_out[1], in_1[1]);
  not not_3 (not_1_out[2], in_1[2]);
  not not_4 (not_1_out[3], in_1[3]);
  add_4 add_4_1 (.in_2(not_1_out), .Overflow(in_2), .in_1(4'b0001), .out_4(S__Resultado));
endmodule

module subtrator (
  input  [3:0] in_1,
  input  in_2,
  input  [3:0] in_3,
  input  in_4,
  output [3:0] out_5
);

  wire [3:0] compl_2_1_s__resultado;

  add_4 add_4_1 (.in_2(in_3), .Overflow(in_4), .in_1(compl_2_1_s__resultado), .out_4(out_5));
  COMPL_2 compl_2_1 (.in_1(in_1), .in_2(in_2), .S__Resultado(compl_2_1_s__resultado));
endmodule
