// Logisim project circuito_jurados.circ as structural Verilog: 2 circuits, main circuit main
module main (
  input  in_1,
  input  in_2,
  input  in_3,
  input  in_4
);

  wire mion_1_out_5;

  MION mion_1 (.in_1(in_1), .in_2(in_2), .in_3(in_3), .in_4(in_4), .out_5(mion_1_out_5));
  LED led_1 (.in(mion_1_out_5));
endmodule

module MION (
  input  in_1,
  input  in_2,
  input  in_3,
  input  in_4,
  output out_5
);

  wire AB_nC_D_out, ABC_nD_out, ABCD_out, and_1_out, and_2_out;

  and and_1 (and_1_out, ~in_4, in_3, in_2, in_1);  // AND_Gate
  and and_2 (and_2_out, in_4, ~in_3, in_2, in_1);  // AND_Gate
  and AB_nC_D (AB_nC_D_out, in_4, in_3, ~in_2, in_1);  // AND_Gate
  and ABC_nD (ABC_nD_out, in_4, in_3, in_2, ~in_1);  // AND_Gate
  and ABCD (ABCD_out, in_4, in_3, in_2, in_1);
  or \or  (out_5, and_1_out, and_2_out, AB_nC_D_out, ABC_nD_out, ABCD_out);

  // Notes on the sheet:
  //   (~A)BCD
  //   A(~B)CD
endmodule
